// Logisim project meio somador.circ as structural Verilog: 1 circuit, main circuit main
module main (
  input  A,
  input  B,
  output VAI_UM,
  output out_4
);

  wire and_2_out, and_3_out, not_1_out, not_2_out;

  not not_1 (not_1_out, A);
  not not_2 (not_2_out, B);
  and and_1 (VAI_UM, A, B);
  and and_2 (and_2_out, not_1_out, B);
  and and_3 (and_3_out, A, not_2_out);
  or or_1 (out_4, and_2_out, and_3_out);
endmodule
