// Logisim project multplexador.circ as structural Verilog: 1 circuit, main circuit main
module main (
  input  A,
  input  B,
  input  C0,
  input  C1,
  input  C0_2,
  input  C1_2,
  output COMP0,
  output COMP1,
  output COMP2,
  output COMP3
);

  wire and_2_out, and_3_out, and_4_out, and_5_out, and_6_out, and_7_out, and_8_out, and_9_out, and_10_out,
       AND_out, not_1_out, not_2_out, not_3_out, not_4_out, not_5_out, not_6_out, not_7_out, not_8_out,
       not_9_out, not_10_out, or_2_out, OR_out, PE_out, SOMA_out;

  not not_1 (not_1_out, A);
  not not_2 (not_2_out, B);
  and AND (AND_out, A, B);
  and and_2 (and_2_out, not_1_out, B);
  and and_3 (and_3_out, A, not_2_out);
  and and_4 (and_4_out, A, B);
  and and_5 (and_5_out, not_1_out, B);
  and and_6 (and_6_out, A, not_2_out);
  and PE (PE_out, not_1_out, B);
  or OR (OR_out, and_2_out, and_3_out, and_4_out);
  or SOMA (SOMA_out, and_5_out, and_6_out);
  not not_3 (not_3_out, C0_2);
  not not_4 (not_4_out, C1_2);
  and and_7 (and_7_out, OR_out, not_5_out, C1_2);
  not not_5 (not_5_out, C0_2);
  and and_8 (and_8_out, SOMA_out, C0_2, not_6_out);
  not not_6 (not_6_out, C1_2);
  and and_9 (and_9_out, PE_out, C0_2, C1_2);
  and and_10 (and_10_out, AND_out, not_3_out, not_4_out);
  or or_2 (or_2_out, and_10_out, and_7_out, and_8_out, and_9_out);
  not not_7 (not_7_out, C0);
  not not_8 (not_8_out, C1);
  not not_9 (not_9_out, C0);
  not not_10 (not_10_out, C1);
  and and_11 (COMP0, or_2_out, not_7_out, not_8_out);
  and and_12 (COMP1, or_2_out, not_9_out, C1);
  and and_13 (COMP2, or_2_out, C0, not_10_out);
  and and_14 (COMP3, or_2_out, C0, C1);

  // Notes on the sheet:
  //   *MULTIPLEXADOR*
  //   *DEMULTIPLEXADOR*
endmodule
