// Logisim project somador completo.circ as structural Verilog: 2 circuits, main circuit Somador completo
module Somador_completo (
  input  A,
  input  B,
  input  V,
  output SOMA,
  output VAI_UM
);

  wire and_1_out, and_2_out, and_3_out, and_4_out, and_5_out, and_6_out, and_7_out, and_8_out, not_1_out,
       not_2_out, not_3_out, not_4_out, not_5_out, not_6_out, not_7_out, not_8_out, not_9_out;

  not not_1 (not_1_out, A);
  not not_2 (not_2_out, B);
  not not_3 (not_3_out, A);
  not not_4 (not_4_out, V);
  not not_5 (not_5_out, B);
  not not_6 (not_6_out, V);
  not not_7 (not_7_out, A);
  not not_8 (not_8_out, B);
  not not_9 (not_9_out, V);
  and and_1 (and_1_out, not_1_out, not_2_out, V);
  and and_2 (and_2_out, not_3_out, B, not_4_out);
  and and_3 (and_3_out, A, not_5_out, not_6_out);
  and and_4 (and_4_out, A, B, V);
  and and_5 (and_5_out, not_7_out, B, V);
  and and_6 (and_6_out, A, not_8_out, V);
  and and_7 (and_7_out, A, B, not_9_out);
  and and_8 (and_8_out, A, B, V);
  or or_1 (SOMA, and_1_out, and_2_out, and_3_out, and_4_out);
  or or_2 (VAI_UM, and_5_out, and_6_out, and_7_out, and_8_out);
endmodule

module caderno (
  input  V1,
  input  B1,
  input  B2,
  input  A1,
  input  A2,
  output SOMA,
  output SOMA_2,
  output VAI_UM,
  output VAI_UM_2
);

  Somador_completo somador_completo_1 (.A(A1), .B(B1), .V(V1), .SOMA(SOMA), .VAI_UM(VAI_UM));
  Somador_completo somador_completo_2 (.A(A2), .B(B2), .V(VAI_UM), .SOMA(SOMA_2), .VAI_UM(VAI_UM_2));
endmodule
